# Fritzing sketch Dijital Metre (saved by Fritzing 0.9.5d)

parts:
  LCD1 = LCD screen
  Parça1 = Arduino Uno (Rev3)
  hc-sr1 = hc-sr04
  R1 = Rotary Potentiometer (Small) [maximum_resistance=100kΩ package=THT]

nets:
  GND: LCD1.VSS, LCD1.R/W, Parça1.GND, hc-sr1.GND, R1.leg1
  VDD: LCD1.VDD, Parça1.5V, hc-sr1.VCC, R1.leg2
  N1: LCD1.V0, R1.wiper
  N2: LCD1.RS, Parça1.D7
  N3: LCD1.DB4, Parça1.D5_PWM
  N4: LCD1.DB5, Parça1.D4
  N5: LCD1.DB6, Parça1.D3_PWM
  N6: LCD1.DB7, Parça1.D2
  N7: Parça1.D8, hc-sr1.Echo
  N8: Parça1.D9_PWM, hc-sr1.Trig
